# Fritzing sketch XL4016X2 (saved by Fritzing 0.9.3b)
perfboards: 3

parts:
  J1 = Screw terminal - 2 pins [package=THT]
  D2 = TVS Diode 47V [part_number=P6KE47CA]
  R1 = Resistor [tolerance=±5% resistance=100k package=THT]
  R2 = Resistor [tolerance=±5% resistance=15k package=THT]
  C1 = Ceramic Capacitor [capacitance=100nF package="100 mil [THT, multilayer]"]
  Part1 = ACS712 Low Current Sensor Board v12
  C2 = Electrolytic Capacitor [capacitance=0.1mF package="100 mil [THT, electrolytic]"]
  C3 = Electrolytic Capacitor [capacitance=0.1mF package="100 mil [THT, electrolytic]"]
  C4 = Electrolytic Capacitor [capacitance=0.1mF package="100 mil [THT, electrolytic]"]
  C5 = Electrolytic Capacitor [capacitance=0.1mF package="100 mil [THT, electrolytic]"]
  J2 = Screw terminal - 2 pins [package=THT]
  R3 = Resistor [tolerance=±5% resistance=100k package=THT]
  R4 = Resistor [tolerance=±5% resistance=47k package=THT]
  Part2 = ACS712 Low Current Sensor Board v12
  C6 = Ceramic Capacitor [capacitance=100nF package="100 mil [THT, multilayer]"]
  Fuse1 = Fuse with Handler [part_number=Htc-15m]
  J3 = Screw terminal - 2 pins [package=THT]
  J4 = Screw terminal - 2 pins [package=THT]  # not connected

nets (from the breadboard view):
  N1: J1.pin1, D2.anode
  N2: J1.pin2, D2.cathode
  N3: R1.Pin_0, R2.Pin_1, C1.0
  N4: R2.Pin_0, C1.1, Part1.GND, C2.-, C4.-
  N5: Part1.IP+, C2.+, C3.+, C4.+, C5.+
  N6: C3.-, C5.-
  N7: J2.pin1, R4.Pin_0, Part2.GND, C6.1
  N8: J2.pin2, Fuse1.Connector1
  N9: R3.Pin_0, R4.Pin_1, C6.0
  N10: R3.Pin_1, Fuse1.Connector2
  N11: Part2.5V, J3.pin2

notes:
  Battery terminal
  +5V from MP2307 buck
  Solar Panel terminal
  +5V from MP2307 buck converter
  Vbb to MP2307 buck converter

custom parts:
  TVS Diode 47V: A transient voltage suppressor diode
